# Fritzing sketch PO-Teensy-MIDI-Sync-FastLED (saved by Fritzing 0.9.3b)
breadboards: 1

parts:
  TRS1 = Audio Jack (TRS) 3.5mm [package="PG203J [THT]"]
  Teensy_3_1 = Teensy 3.1
  NEOPIXEL3 = Neopixel Strip -- White (60/m)
  J3 = Power Jack [package=power_jack_combo]
  S1 = Momentary Switch [package=ksa_sealed_tac_switch]
  S2 = Momentary Switch [package=ksa_sealed_tac_switch]
  S3 = Momentary Switch [package=ksa_sealed_tac_switch]
  S4 = Momentary Switch [package=ksa_sealed_tac_switch]
  S5 = Momentary Switch [package=ksa_sealed_tac_switch]
  S6 = Momentary Switch [package=ksa_sealed_tac_switch]
  S7 = Momentary Switch [package=ksa_sealed_tac_switch]
  S8 = Momentary Switch [package=ksa_sealed_tac_switch]
  R1 = Rotary Potentiometer (Small) [maximum_resistance=100kΩ package=THT]
  R2 = Rotary Potentiometer (Small) [maximum_resistance=100kΩ package=THT]
  R3 = Rotary Potentiometer (Small) [maximum_resistance=100kΩ package=THT]
  R4 = Rotary Potentiometer (Small) [maximum_resistance=100kΩ package=THT]
  R5 = Rotary Potentiometer (Small) [maximum_resistance=100kΩ package=THT]
  R6 = Rotary Potentiometer (Small) [maximum_resistance=100kΩ package=THT]
  R7 = Rotary Potentiometer (Small) [maximum_resistance=100kΩ package=THT]
  R8 = Rotary Potentiometer (Small) [maximum_resistance=100kΩ package=THT]

nets:
  N1: TRS1.Sleeve, Teensy_3_1.GND
  N2: TRS1.Tip, Teensy_3_1.D0
  N3: Teensy_3_1.D1, NEOPIXEL3.+5V
  N4: Teensy_3_1.D2, S1.3
  N5: Teensy_3_1.D3, S2.3
  N6: Teensy_3_1.D8, S8.3
  N7: Teensy_3_1.A2/D16, S5.3
  N8: Teensy_3_1.A3/D17, S4.3
  N9: Teensy_3_1.A6/D20, S3.3
  N10: Teensy_3_1.A7/D21, S7.3
  N11: NEOPIXEL3.DI, J3.PWR
  GND: NEOPIXEL3.GND, J3.GND
  N12: S1.1, S2.1, S3.1, S4.1, S5.1, S6.1, S7.1, S8.1
  N13: S1.2, R1.wiper
  N14: S2.2, R2.leg1
  N15: S2.4, R2.leg2
  N16: S3.2, R5.wiper
  N17: S4.2, R6.leg1
  N18: S4.4, R6.leg2
  N19: S5.2, R7.wiper
  N20: S6.2, R3.leg1
  N21: S6.4, R3.leg2
  N22: S7.2, R4.leg1
  N23: S7.4, R4.leg2
  N24: S8.2, R8.leg1
  N25: S8.4, R8.leg2

custom parts:
  Neopixel Strip -- White (60/m): Neopixel Strip, White, 60 pixels per meter.
  Power Jack: Power Jack This is the standard 5.5mm barrel jack for power. The PTH is the most common, proven, reliable, footprint. All others are experimental. The Slot footprint only works if the mill layer is transmitted to the PCB fab house so be warned. Spark Fun Electronics SKU : PRT-00119. Mating wall wart : TOL-00298 (and others)
